// Logisim project 19CS020078085CLONE.circ as structural Verilog: 1 circuit, main circuit main
module main (
  input  [3:0] ADDRESSC,
  input  [3:0] OPCODE,
  input  [3:0] Ri_ADDRESS,
  input  [3:0] Rj_ADDRESS,
  input  [3:0] Rk_ADDRESS,
  input  [15:0] IMMEDIATE,
  input  in_7,
  input  in_8,
  input  in_9,
  output [15:0] out_10
);

  wire ADD, ADI, AND, ANI, button_1_out, button_2_out, clktunnel, demultiplexer_1_out13,
       demultiplexer_1_out14, demultiplexer_1_out15, HLT, LOAD, MOVE, MUXA_TUN, MUXB_TUN, MVI, OR, or_1_out,
       or_2_out, or_3_out, or_5_out, ORI, PCENABLE, R1E, R2E, R3E, R4E, R5E, R6E, R7E, R8E, R9E, R10E, R11E,
       R12E, R13E, R14E, R15E, R16E, S2, S3, S4, S5, shift_register_1_out, shift_register_2_out, STORE, SUB,
       SUI;
  wire [3:0] ADDRESSA, ADDRESSB;
  wire [15:0] bit_extender_2_out, IMEEDIATE_TUN, MEMORYDATA, multiplexer_6_out;
  wire [31:0] BOTH, DIFF, INPUTTORGTF, MEMORYADDRESS, multiplexer_1_out, multiplexer_2_out,
       multiplexer_3_out, ORR, R1O, R2O, R3O, R4O, R5O, R6O, R7O, R8O, R9O, R10O, R11O, R12O, R13O, R14O,
       R15O, R16O, RAin, RB_q, RBin, RZin, SUM, undriven;

  Button button_1 (.out(button_1_out));
  Register #(.width(32)) RZ (.D(RZin), .Q(MEMORYADDRESS), .clk(clktunnel));  // open: en, clr
  Multiplexer #(.width(32)) multiplexer_1 (
    .in0(MEMORYADDRESS), .in1({IMEEDIATE_TUN, MEMORYDATA}), .out(multiplexer_1_out));  // open: sel, en
  Demultiplexer #(.select(4)) demultiplexer_1 (
    .out0(MOVE), .out1(MVI), .out2(LOAD), .out3(STORE), .out4(ADD), .out5(ADI), .out6(SUB), .out7(SUI),
    .out8(AND), .out9(ANI), .out10(OR), .out11(ORI), .out12(HLT), .out13(demultiplexer_1_out13),
    .out14(demultiplexer_1_out14), .out15(demultiplexer_1_out15), .in(1'b1), .sel(MEMORYDATA[3:0]));  // open: en
  Register #(.width(32)) RY (.D(multiplexer_1_out), .Q(INPUTTORGTF), .clk(clktunnel));  // open: en, clr
  Register #(.width(32)) R1 (.D(INPUTTORGTF), .en(R1E), .Q(R1O), .clk(clktunnel), .clr(button_1_out));
  Register #(.width(32)) R9 (.D(INPUTTORGTF), .en(R9E), .Q(R9O), .clk(clktunnel), .clr(button_1_out));
  Multiplexer #(.select(4), .width(32)) multiplexer_2 (
    .in0(R1O), .in1(R2O), .in2(R3O), .in3(R4O), .in4(R5O), .in5(R6O), .in6(R7O), .in7(R8O), .in8(R9O),
    .in9(R10O), .in10(R11O), .in11(R12O), .in12(R13O), .in13(R14O), .in14(R15O), .in15(R16O),
    .out(multiplexer_2_out), .sel(ADDRESSA), .en(MUXA_TUN));
  or or_1 (or_1_out, MOVE, LOAD, STORE, ADD, ADI, SUB, SUI, AND, ANI, OR, ORI);
  Register #(.width(32)) R2 (.D(INPUTTORGTF), .en(R2E), .Q(R2O), .clk(clktunnel), .clr(button_1_out));
  Register #(.width(32)) RA (.D(multiplexer_2_out), .Q(RAin), .clk(clktunnel));  // open: en, clr
  Register #(.width(32)) R10 (.D(INPUTTORGTF), .en(R10E), .Q(R10O), .clk(clktunnel), .clr(button_1_out));
  and and_1 (MUXA_TUN, S2, or_1_out);
  Register #(.width(32)) R3 (.D(INPUTTORGTF), .en(R3E), .Q(R3O), .clk(clktunnel), .clr(button_1_out));
  Register #(.width(32)) R11 (.D(INPUTTORGTF), .en(R11E), .Q(R11O), .clk(clktunnel), .clr(button_1_out));
  Counter #(.width(16), .max('hffff)) counter_1 (
    .count(PCENABLE), .Q(out_10), .clk(clktunnel), .clr(button_2_out));  // open: load, D, carry
  Register #(.width(32)) R4 (.D(INPUTTORGTF), .en(R4E), .Q(R4O), .clk(clktunnel), .clr(button_1_out));
  Register #(.width(32)) R12 (.D(INPUTTORGTF), .en(R12E), .Q(R12O), .clk(clktunnel), .clr(button_1_out));
  Button button_2 (.out(button_2_out));
  Register #(.width(32)) R5 (.D(INPUTTORGTF), .en(R5E), .Q(R5O), .clk(clktunnel), .clr(button_1_out));
  Register #(.width(32)) R13 (.D(INPUTTORGTF), .en(R13E), .Q(R13O), .clk(clktunnel), .clr(button_1_out));
  Shift_Register #(.length(6)) shift_register_1 (
    .in(shift_register_1_out), .clk(clktunnel), .out(shift_register_1_out), .q1(PCENABLE));  // open: shift, load, clr, d0, q0, d1, d2, q2, d3, q3, d4, q4, d5, q5
  Shift_Register #(.length(6)) shift_register_2 (
    .in(shift_register_2_out), .clk(clktunnel), .out(shift_register_2_out), .q1(S2), .q2(S3), .q3(S4), .q4(S5));  // open: shift, load, clr, d0, q0, d1, d2, d3, d4, d5, q5
  Register #(.width(32)) R6 (.D(INPUTTORGTF), .en(R6E), .Q(R6O), .clk(clktunnel), .clr(button_1_out));
  Register #(.width(32)) R14 (.D(INPUTTORGTF), .en(R14E), .Q(R14O), .clk(clktunnel), .clr(button_1_out));
  Multiplexer #(.select(4), .width(32)) multiplexer_3 (
    .in0(R1O), .in1(R2O), .in2(R3O), .in3(R4O), .in4(R5O), .in5(R6O), .in6(R7O), .in7(R8O), .in8(R9O),
    .in9(R10O), .in10(R11O), .in11(R12O), .in12(R13O), .in13(R14O), .in14(R15O), .in15(R16O),
    .out(multiplexer_3_out), .sel(ADDRESSB), .en(MUXB_TUN));
  Register #(.width(32)) RB (.D(multiplexer_3_out), .Q(RB_q), .clk(clktunnel));  // open: en, clr
  Multiplexer #(.width(32)) multiplexer_4 (.in0(RB_q), .in1(undriven), .out(RBin));  // open: sel, en
  or or_2 (or_2_out, ADD, SUB, AND, OR);
  Register #(.width(32)) R7 (.D(INPUTTORGTF), .en(R7E), .clk(clktunnel), .clr(button_1_out));  // open: Q
  Register #(.width(32)) R15 (.D(INPUTTORGTF), .en(R15E), .Q(R15O), .clk(clktunnel), .clr(button_1_out));
  Clock clk (.out(clktunnel));
  and and_2 (MUXB_TUN, S2, or_2_out);
  Bit_Extender #(.in_width(32)) bit_extender_1 (.in(undriven));  // open: out
  Register #(.width(32)) R8 (.D(INPUTTORGTF), .en(R8E), .clk(clktunnel), .clr(button_1_out));  // open: Q
  Register #(.width(32)) R16 (.D(INPUTTORGTF), .en(R16E), .Q(R16O), .clk(clktunnel), .clr(button_1_out));
  // Probe on {IMMEDIATE, Rk_ADDRESS, Rj_ADDRESS, Ri_ADDRESS, OPCODE}
  Demultiplexer #(.select(4)) demultiplexer_2 (
    .out0(R1E), .out1(R2E), .out2(R3E), .out3(R4E), .out4(R5E), .out5(R6E), .out6(R7E), .out7(R8E),
    .out8(R9E), .out9(R10E), .out10(R11E), .out11(R12E), .out12(R13E), .out13(R14E), .out14(R15E),
    .out15(R16E), .in(1'b1), .sel(ADDRESSC));  // open: en
  or or_3 (or_3_out, MOVE, LOAD, STORE, ADD, ADI, SUB, SUI, AND, ANI, OR, ORI);
  Multiplexer #(.width(4)) multiplexer_5 (
    .in0(4'b0000), .in1(MEMORYDATA[11:8]), .out(ADDRESSA), .sel(1'b1), .en(or_3_out));
  Subtractor #(.width(32)) subtractor_1 (.a(RAin), .b(RBin), .out(DIFF));  // open: bin, bout
  Demultiplexer #(.select(2), .width(32)) demultiplexer_3 (
    .out0(SUM), .out1(DIFF), .out2(BOTH), .out3(ORR), .in(RZin));  // open: sel, en
  Adder #(.width(32)) adder_1 (.a(RAin), .b(RBin), .out(SUM));  // open: cin, cout
  assign BOTH = RAin & RBin;  // AND_Gate and_3, 32 bits wide
  assign ORR = RAin | RBin;  // OR_Gate or_4, 32 bits wide
  Bit_Extender #(.in_width(32)) bit_extender_2 (.in(MEMORYADDRESS), .out(bit_extender_2_out));
  Multiplexer #(.width(16)) multiplexer_6 (
    .in0(out_10), .in1(bit_extender_2_out), .out(multiplexer_6_out), .sel(in_9));  // open: en
  or or_5 (or_5_out, ADD, SUB, AND, OR);
  RAM #(.addrWidth(16), .dataWidth(32)) ram_1 (
    .addr(multiplexer_6_out), .data({IMEEDIATE_TUN, MEMORYDATA}), .ld(in_8), .clr(in_7));  // open: sel, clk
  Multiplexer #(.width(4)) multiplexer_7 (
    .in0(4'b0000), .in1(MEMORYDATA[15:12]), .out(ADDRESSB), .sel(1'b1), .en(or_5_out));

  // Other names for the same wires on the sheet: MEMMUX = in_9; Rk_ADDRESS_t[3:0] = MEMORYDATA[15:12];
  //   MEMORYDATA[31:16] = IMEEDIATE_TUN; OPCODETUN[3:0] = MEMORYDATA[3:0]; PC[15:0] = out_10;
  //   Ri_ADDRESS_t[3:0] = MEMORYDATA[7:4]; Rj_ADDRESS_t[3:0] = MEMORYDATA[11:8]

  // Notes on the sheet:
  //   REGISTERFILE
  //   PC
  //   CONTROLSIGNAL
  //   HEXCONVERTOR
  //   ALU
  //   !!NOTE THIS IS JUST FOR CONVERSION PURPOSE 
  //   AFTER Converting we have to enter it into memory
  //   MEMORY
endmodule
